// Logisim project 8bit-CPU.circ as structural Verilog: 9 circuits, main circuit register
module main (
  input  [15:0] in_1,
  input  in_2,
  input  in_3,
  input  in_4
);

  wire button_1_out, clock_1_out, cpu_1_clk_2, cpu_1_out_10, cpu_1_rst_2, cpu_1_str;
  wire [7:0] cpu_1_out_5, cpu_1_out_6, ram_2_data;
  wire [15:0] cpu_1_address, cpu_1_out_12, ram_1_data;

  LED led_1 (.in(cpu_1_out_5[7]));
  LED led_2 (.in(cpu_1_out_5[6]));
  RAM_part #(.addrWidth(16), .dataWidth(16), .bus("separate")) ram_1 (
    .addr(cpu_1_out_12), .din(in_1), .data(ram_1_data), .str(in_2), .sel(1'b1), .clk(in_3), .ld(1'b1),
    .clr(in_4));
  LED led_3 (.in(cpu_1_out_5[4]));
  LED led_4 (.in(cpu_1_out_5[5]));
  Clock clock_1 (.out(clock_1_out));
  Button button_1 (.out(button_1_out));
  LED led_5 (.in(cpu_1_out_5[3]));
  LED led_6 (.in(cpu_1_out_5[1]));
  LED led_7 (.in(cpu_1_out_5[2]));
  LED led_8 (.in(cpu_1_out_10));
  CPU cpu_1 (
    .out_5(cpu_1_out_5), .in_2(ram_1_data), .rst(button_1_out), .clk(clock_1_out), .out_12(cpu_1_out_12),
    .out_6(cpu_1_out_6), .in_1(ram_2_data), .STR(cpu_1_str), .CLK_2(cpu_1_clk_2), .RST_2(cpu_1_rst_2),
    .ADDRESS(cpu_1_address), .out_10(cpu_1_out_10));
  LED led_9 (.in(cpu_1_out_5[0]));
  RAM_part #(.addrWidth(16), .bus("separate")) ram_2 (
    .addr(cpu_1_address), .din(cpu_1_out_6), .data(ram_2_data), .str(cpu_1_str), .sel(1'b1),
    .clk(cpu_1_clk_2), .ld(1'b1), .clr(cpu_1_rst_2));
endmodule

module register (
  input  [7:0] in_1,
  input  [7:0] in_2,
  input  in_3,
  input  [3:0] in_4,
  input  [2:0] in_5,
  input  in_6,
  input  in_7,
  input  in_8,
  output [7:0] out_9,
  output [7:0] out_10,
  output [7:0] out_11,
  output [7:0] out_12,
  output [7:0] out_13,
  output [7:0] out_14,
  output [7:0] out_15,
  output [3:0] out_16
);

  wire demultiplexer_1_out1, demultiplexer_1_out2, demultiplexer_1_out3, demultiplexer_1_out4,
       demultiplexer_1_out5, demultiplexer_1_out6, demultiplexer_1_out7, multiplexer_2_out;
  wire [7:0] multiplexer_1_out;

  Demultiplexer #(.select(3), .enable("false")) demultiplexer_1 (
    .out1(demultiplexer_1_out1), .out2(demultiplexer_1_out2), .out3(demultiplexer_1_out3),
    .out4(demultiplexer_1_out4), .out5(demultiplexer_1_out5), .out6(demultiplexer_1_out6),
    .out7(demultiplexer_1_out7), .in(in_6), .sel(in_5));  // open: out0
  Register register_1 (.D(in_1), .en(demultiplexer_1_out1), .Q(out_9), .clk(in_7), .clr(in_8));
  Register register_2 (.D(in_1), .en(demultiplexer_1_out2), .Q(out_10), .clk(in_7), .clr(in_8));
  Register register_3 (.D(in_1), .en(demultiplexer_1_out3), .Q(out_11), .clk(in_7), .clr(in_8));
  Multiplexer #(.width(8), .enable("false")) multiplexer_1 (
    .in0(in_1), .in1(in_2), .out(multiplexer_1_out), .sel(in_3));
  Register register_4 (.D(multiplexer_1_out), .en(multiplexer_2_out), .Q(out_12), .clk(in_7), .clr(in_8));
  Multiplexer #(.enable("false")) multiplexer_2 (
    .in0(demultiplexer_1_out4), .in1(in_3), .out(multiplexer_2_out), .sel(in_3));
  Register register_5 (.D(in_1), .en(demultiplexer_1_out5), .Q(out_13), .clk(in_7), .clr(in_8));
  Register register_6 (.D(in_1), .en(demultiplexer_1_out6), .Q(out_14), .clk(in_7), .clr(in_8));
  Register register_7 (.D(in_1), .en(demultiplexer_1_out7), .Q(out_15), .clk(in_7), .clr(in_8));
  Register #(.width(4)) register_8 (.D(in_4), .en(in_7), .Q(out_16), .clk(in_7), .clr(in_8));

  // Notes on the sheet:
  //   AX
  //   BX
  //   CX
  //   DX
  //   EX
  //   CS
  //   DS
  //   FLAG
endmodule

module RAM (
  input  [15:0] in_1,
  input  [7:0] in_2,
  input  Store_Signal,
  input  in_4,
  input  Clock,
  output [7:0] out_6
);

  RAM_part #(.addrWidth(16), .bus("separate")) ram_1 (
    .addr(in_1), .din(in_2), .data(out_6), .str(Store_Signal), .sel(1'b1), .clk(Clock), .ld(1'b1), .clr(in_4));

  // Notes on the sheet:
  //   Address
  //   Data In
  //   Data Out
endmodule

module ALU (
  input  ADD,
  input  SUB,
  input  MUL,
  input  DIV,
  input  AND,
  input  OR,
  input  XOR,
  input  SHF,
  input  CMP,
  input  NOT,
  input  MOV,
  input  [7:0] in_12,
  input  [7:0] ADD_2,
  output [7:0] out_14,
  output [7:0] out_15,
  output out_16,
  output [3:0] out_17
);

  wire adder_1_cout, controlled_buffer_2_out, not_2_out, not_3_out, not_4_out, or_3_out, subtractor_1_bout,
       xor_2_out, xor_3_out;
  wire [3:0] controlled_buffer_1_out;
  wire [7:0] adder_1_out, and_1_out, controlled_buffer_17_out, divider_1_out, divider_1_rem,
       multiplexer_1_out, multiplier_1_cout, multiplier_1_out, not_1_out, or_1_out, shifter_1_out,
       shifter_2_out, subtractor_1_out, xor_1_out;

  Adder adder_1 (.a(in_12), .b(ADD_2), .out(adder_1_out), .cout(adder_1_cout));  // open: cin
  Subtractor subtractor_1 (.a(in_12), .b(ADD_2), .out(subtractor_1_out), .bout(subtractor_1_bout));  // open: bin
  assign controlled_buffer_1_out[0] = not_4_out ? subtractor_1_bout : 1'bz;  // Controlled_Buffer controlled_buffer_1
  Multiplier multiplier_1 (.a(in_12), .b(ADD_2), .out(multiplier_1_out), .cout(multiplier_1_cout));  // open: cin
  Divider divider_1 (.a(in_12), .b(ADD_2), .out(divider_1_out), .rem(divider_1_rem));  // open: upper
  assign and_1_out = in_12 & ADD_2;  // AND_Gate and_1, 8 bits wide
  assign or_1_out = in_12 | ADD_2;  // OR_Gate or_1, 8 bits wide
  assign xor_1_out = in_12 ^ ADD_2;  // XOR_Gate xor_1, 8 bits wide
  assign not_1_out = ~in_12;  // NOT_Gate not_1, 8 bits wide
  Shifter shifter_1 (.in(in_12), .\dist (ADD_2[2:0]), .out(shifter_1_out));
  Multiplexer #(.width(8), .enable("false")) multiplexer_1 (
    .in0(shifter_1_out), .in1(shifter_2_out), .out(multiplexer_1_out), .sel(ADD_2[3]));
  Shifter #(.shift("ar")) shifter_2 (.in(in_12), .\dist (ADD_2[2:0]), .out(shifter_2_out));
  not not_2 (not_2_out, not_4_out);
  assign controlled_buffer_2_out = not_4_out ? xor_2_out : 1'bz;  // Controlled_Buffer controlled_buffer_2
  xor xor_2 (xor_2_out, in_12[7], ADD_2[7]);
  not not_3 (not_3_out, xor_2_out);
  not not_4 (not_4_out, ADD);
  assign out_14 = ADD ? adder_1_out : 8'bz;  // Controlled_Buffer controlled_buffer_3
  assign controlled_buffer_1_out[0] = ADD ? adder_1_cout : 1'bz;  // Controlled_Buffer controlled_buffer_4
  assign out_14 = SUB ? subtractor_1_out : 8'bz;  // Controlled_Buffer controlled_buffer_5
  assign out_14 = MUL ? multiplier_1_out : 8'bz;  // Controlled_Buffer controlled_buffer_6
  assign out_15 = MUL ? multiplier_1_cout : 8'bz;  // Controlled_Buffer controlled_buffer_7
  assign out_14 = DIV ? divider_1_out : 8'bz;  // Controlled_Buffer controlled_buffer_8
  assign out_15 = DIV ? divider_1_rem : 8'bz;  // Controlled_Buffer controlled_buffer_9
  assign out_14 = AND ? and_1_out : 8'bz;  // Controlled_Buffer controlled_buffer_10
  assign out_14 = OR ? or_1_out : 8'bz;  // Controlled_Buffer controlled_buffer_11
  assign out_14 = XOR ? xor_1_out : 8'bz;  // Controlled_Buffer controlled_buffer_12
  assign out_14 = SHF ? multiplexer_1_out : 8'bz;  // Controlled_Buffer controlled_buffer_13
  assign out_14 = NOT ? not_1_out : 8'bz;  // Controlled_Buffer controlled_buffer_14
  assign out_14 = CMP ? in_12 : 8'bz;  // Controlled_Buffer controlled_buffer_15
  assign out_15 = CMP ? ADD_2 : 8'bz;  // Controlled_Buffer controlled_buffer_16
  assign controlled_buffer_17_out = not_4_out ? subtractor_1_out : 8'bz;  // Controlled_Buffer controlled_buffer_17
  assign controlled_buffer_17_out = not_2_out ? adder_1_out : 8'bz;  // Controlled_Buffer controlled_buffer_18
  assign controlled_buffer_2_out = not_2_out ? not_3_out : 1'bz;  // Controlled_Buffer controlled_buffer_19
  assign out_14 = MOV ? ADD_2 : 8'bz;  // Controlled_Buffer controlled_buffer_20
  Pull_Resistor pull_resistor_1 (.node(out_14));
  Pull_Resistor pull_resistor_2 (.node(controlled_buffer_1_out[0]));
  Pull_Resistor pull_resistor_3 (.node(out_15));
  or or_2 (out_16, MUL, DIV);
  nor nor_1 (controlled_buffer_1_out[1], controlled_buffer_17_out[0], controlled_buffer_17_out[1], controlled_buffer_17_out[2], controlled_buffer_17_out[3], controlled_buffer_17_out[4], controlled_buffer_17_out[5], controlled_buffer_17_out[6], controlled_buffer_17_out[7]);
  xor xor_3 (xor_3_out, controlled_buffer_17_out[7], in_12[7]);
  and and_2 (controlled_buffer_1_out[3], xor_3_out, controlled_buffer_2_out);
  or or_3 (or_3_out, ADD, SUB, CMP);
  assign out_17 = or_3_out ? {controlled_buffer_1_out[3], controlled_buffer_17_out[7], controlled_buffer_1_out[1:0]} : 4'bz;  // Controlled_Buffer controlled_buffer_21

  // Notes on the sheet:
  //   0000
  //   SUB
  //   0001
  //   MUL
  //   0010
  //   DIV
  //   0011
  //   0100
  //   AND
  //   OR
  //   0101
  //   0110
  //   XOR
  //   0111
  //   SHF
  //   C
  //   Z
  //   S
  //   O
endmodule

module \cross  (
  input  [2:0] in_1,
  input  [2:0] in_2,
  input  in_3,
  output [2:0] out_4,
  output [2:0] out_5
);

  wire not_1_out, not_2_out;

  assign out_5 = in_3 ? in_1 : 3'bz;  // Controlled_Buffer controlled_buffer_1
  assign out_4 = not_1_out ? in_1 : 3'bz;  // Controlled_Buffer controlled_buffer_2
  not not_1 (not_1_out, in_3);
  assign out_4 = in_3 ? in_2 : 3'bz;  // Controlled_Buffer controlled_buffer_3
  assign out_5 = not_2_out ? in_2 : 3'bz;  // Controlled_Buffer controlled_buffer_4
  not not_2 (not_2_out, in_3);
endmodule

module instru_ram (
  input  [15:0] in_1,
  input  [15:0] in_2,
  input  Store_Signal,
  input  in_4,
  input  Clock,
  output [15:0] out_6
);

  RAM_part #(.addrWidth(16), .dataWidth(16), .bus("separate")) ram_1 (
    .addr(in_1), .din(in_2), .data(out_6), .str(Store_Signal), .sel(1'b1), .clk(Clock), .ld(1'b1), .clr(in_4));

  // Notes on the sheet:
  //   Address
  //   Data In
  //   Data Out
endmodule

module clock (
  input  in_1,
  input  in_2,
  output out_3,
  output out_4,
  output out_5,
  output out_6
);

  wire and_1_out, and_2_out, and_3_out, and_4_out, buffer_1_out, buffer_2_out, buffer_3_out, buffer_4_out,
       buffer_5_out, buffer_6_out, buffer_7_out, buffer_8_out, buffer_9_out, buffer_10_out, d_ff_1_q,
       d_ff_1_qn, not_1_out, not_2_out, not_3_out;

  Pull_Resistor pull_resistor_1 (.node(out_3));
  assign out_3 = not_1_out ? and_1_out : 1'bz;  // Controlled_Buffer controlled_buffer_1
  Pull_Resistor pull_resistor_2 (.node(out_5));
  assign out_5 = not_1_out ? and_2_out : 1'bz;  // Controlled_Buffer controlled_buffer_2
  buf buffer_1 (buffer_1_out, buffer_2_out);
  and and_1 (and_1_out, buffer_1_out, d_ff_1_qn);
  and and_2 (and_2_out, d_ff_1_qn, not_2_out);
  buf buffer_2 (buffer_2_out, buffer_5_out);
  buf buffer_3 (buffer_3_out, in_1);
  buf buffer_4 (buffer_4_out, buffer_3_out);
  buf buffer_5 (buffer_5_out, buffer_4_out);
  not not_1 (not_1_out, in_2);
  buf buffer_6 (buffer_6_out, in_1);
  D_Flip_Flop d_ff_1 (
    .clk(in_1), .D(d_ff_1_qn), .Q(d_ff_1_q), .Qn(d_ff_1_qn), .preset(1'b0), .en(not_1_out), .reset(in_2));
  not not_2 (not_2_out, in_1);
  not not_3 (not_3_out, in_2);
  buf buffer_7 (buffer_7_out, buffer_9_out);
  buf buffer_8 (buffer_8_out, buffer_7_out);
  buf buffer_9 (buffer_9_out, buffer_10_out);
  buf buffer_10 (buffer_10_out, buffer_6_out);
  and and_3 (and_3_out, buffer_8_out, d_ff_1_q);
  assign out_6 = not_3_out ? and_4_out : 1'bz;  // Controlled_Buffer controlled_buffer_3
  and and_4 (and_4_out, d_ff_1_q, not_2_out);
  Pull_Resistor pull_resistor_3 (.node(out_4));
  assign out_4 = not_3_out ? and_3_out : 1'bz;  // Controlled_Buffer controlled_buffer_4
  Pull_Resistor pull_resistor_4 (.node(out_6));
endmodule

module CU (
  input  [15:0] in_1,
  input  in_2,
  output out_3
);

  wire _1, _2, _3, _4, add, add_t, all_0, all_1, alu_1_out_16, \and , and_1_out, and_2_out, and_3_out,
       and_6_out, and_7_out, and_8_out, and_9_out, and_10_out, and_11_out, and_t, buffer_6_out, buffer_7_out,
       button_1_out, button_2_out, clock_1_out, cmp, cmp_t, controlled_buffer_24_out, dire, dire_t, div,
       div_t, imme, imme_t, je, jg, jl, jmp, jmp_t, mov, mul, mul_t, nor_1_out, nor_2_out, nor_3_out, \not ,
       not_2_out, not_3_out, not_4_out, not_5_out, not_6_out, not_7_out, not_8_out, not_9_out, not_10_out,
       not_11_out, not_t, \or , or_1_out, or_2_out, or_3_out, or_4_out, or_5_out, or_6_out, or_7_out,
       or_8_out, or_t, prt, ram1, ram2, register_4_q, register_7_q, rst, set, shf, shf_t, str, sub, sub_t,
       ujg, ujl, xnor_1_out, xnor_2_out, \xor , xor_1_out, xor_t;
  wire [2:0] opcode_2, opcode_2_t, reg_1, reg_1_t, reg_2;
  wire [3:0] alu_1_out_17, controlled_buffer_5_out, not_1_out, register_6_out_16;
  wire [7:0] addr, addr_t, alu_1_out_14, alu_1_out_15, controlled_buffer_3_out, controlled_buffer_8_out,
       controlled_buffer_9_out, controlled_buffer_10_out, controlled_buffer_15_out, controlled_buffer_18_out,
       controlled_buffer_19_out, controlled_buffer_22_out, controlled_buffer_23_out, cs, data_in, data_out,
       ip, multiplexer_1_out, multiplexer_2_out, num, num_t, register_1_q, register_2_q, register_3_q,
       register_5_q, register_6_out_9, register_6_out_10, register_6_out_11, register_6_out_12,
       register_6_out_13, register_6_out_14;
  wire [15:0] instruction;
  wire [15:8] data_addr;

  Button button_1 (.out(button_1_out));
  RAM_part #(.addrWidth(16), .dataWidth(16), .bus("separate")) ram_1 (
    .addr({cs, ip}), .din(in_1), .data({instruction[15:12], dire, instruction[10:0]}), .str(in_2),
    .sel(1'b1), .clk(button_1_out), .ld(1'b1), .clr(button_2_out));
  Button button_2 (.out(button_2_out));
  LED led_1 (.in(register_1_q[6]));
  LED led_2 (.in(register_1_q[7]));
  Button button_3 (.out(rst));
  Clock clock_1 (.out(clock_1_out));
  LED led_3 (.in(register_1_q[4]));
  LED led_4 (.in(register_1_q[3]));
  LED led_5 (.in(register_1_q[5]));
  assign not_1_out = ~instruction[15:12];  // NOT_Gate not_1, 4 bits wide
  LED led_6 (.in(register_1_q[1]));
  LED led_7 (.in(register_1_q[2]));
  assign addr = xnor_1_out ? instruction[7:0] : 8'bz;  // Controlled_Buffer controlled_buffer_1
  assign num = imme_t ? instruction[7:0] : 8'bz;  // Controlled_Buffer controlled_buffer_2
  xnor xnor_1 (xnor_1_out, imme_t, all_0);
  assign controlled_buffer_3_out = all_0 ? instruction[7:0] : 8'bz;  // Controlled_Buffer controlled_buffer_3
  not not_2 (not_2_out, all_1);
  assign opcode_2 = all_1 ? instruction[10:8] : 3'bz;  // Controlled_Buffer controlled_buffer_4
  assign controlled_buffer_5_out = xnor_2_out ? instruction[15:12] : 4'bz;  // Controlled_Buffer controlled_buffer_5
  xnor xnor_2 (xnor_2_out, all_1, all_0);
  LED led_8 (.in(register_1_q[0]));
  Pull_Resistor pull_resistor_1 (.node(addr));
  assign reg_2 = controlled_buffer_3_out[2:0];  // Buffer buffer_1, 3 bits wide
  assign controlled_buffer_5_out = controlled_buffer_3_out[7:4];  // Buffer buffer_2, 4 bits wide
  Pull_Resistor pull_resistor_2 (.node(reg_1));
  assign reg_1 = not_2_out ? instruction[10:8] : 3'bz;  // Controlled_Buffer controlled_buffer_6
  buf buffer_3 (all_0, and_1_out);
  and and_1 (and_1_out, not_1_out[0], not_1_out[1], not_1_out[2], not_1_out[3]);
  buf buffer_4 (all_1, and_2_out);
  and and_2 (and_2_out, instruction[12], instruction[13], instruction[14], instruction[15]);
  and and_3 (and_3_out, instruction[12], instruction[14], instruction[15]);
  buf buffer_5 (imme, and_3_out);
  Register register_1 (.D(data_in), .en(prt), .Q(register_1_q), .clk(_4), .clr(rst));
  and and_4 (ram2, controlled_buffer_3_out[3], all_0);
  and and_5 (ram1, dire, all_0);
  Pull_Resistor pull_resistor_3 (.node(controlled_buffer_5_out));
  Decoder #(.select(4), .enable("false")) decoder_1 (
    .out1(add), .out2(sub), .out3(mul), .out4(div), .out5(\and ), .out6(\or ), .out7(\xor ), .out8(shf),
    .out9(cmp), .out10(mov), .out11(\not ), .out12(prt), .out13(set), .sel(controlled_buffer_5_out));  // open: out0, out14, out15
  Register register_2 (.D(data_in), .en(_3), .Q(register_2_q), .clk(_3), .clr(rst));
  Register register_3 (.D(controlled_buffer_8_out), .en(_3), .Q(register_3_q), .clk(_3), .clr(rst));
  ALU alu_1 (
    .in_12(register_2_q), .ADD_2(register_3_q), .out_14(alu_1_out_14), .out_15(alu_1_out_15),
    .out_16(alu_1_out_16), .ADD(add_t), .SUB(sub_t), .MUL(mul_t), .DIV(div_t), .AND(and_t), .OR(or_t),
    .XOR(xor_t), .SHF(shf_t), .CMP(cmp_t), .NOT(not_t), .out_17(alu_1_out_17), .MOV(or_1_out));
  or or_1 (or_1_out, set, prt, mov);
  Pull_Resistor pull_resistor_4 (.node(opcode_2_t));
  Decoder #(.select(3), .enable("false")) decoder_2 (
    .out1(jmp), .out2(je), .out3(jg), .out4(jl), .out5(ujg), .out6(ujl), .sel(opcode_2_t));  // open: out0, out7
  clock clock_2 (.out_5(_4), .out_4(_1), .out_3(_3), .out_6(_2), .in_2(rst), .in_1(clock_1_out));
  Register #(.width(1)) register_4 (.D(1'b1), .en(_3), .Q(register_4_q), .clk(_3), .clr(_4));
  assign data_in = buffer_6_out ? alu_1_out_14 : 8'bz;  // Controlled_Buffer controlled_buffer_7
  buf buffer_6 (buffer_6_out, register_4_q);
  assign controlled_buffer_8_out = or_3_out ? num_t : 8'bz;  // Controlled_Buffer controlled_buffer_8
  or or_2 (or_2_out, prt, dire_t);
  Register register_5 (.D(controlled_buffer_10_out), .en(_4), .Q(register_5_q), .clk(_4), .clr(rst));
  assign controlled_buffer_9_out = not_3_out ? register_5_q : 8'bz;  // Controlled_Buffer controlled_buffer_9
  assign controlled_buffer_10_out = or_4_out ? controlled_buffer_8_out : 8'bz;  // Controlled_Buffer controlled_buffer_10
  not not_3 (not_3_out, rst);
  or or_3 (or_3_out, set, all_1);
  not not_4 (not_4_out, or_2_out);
  not not_5 (not_5_out, or_4_out);
  assign controlled_buffer_9_out = rst ? {8{1'b1}} : 8'bz;  // Controlled_Buffer controlled_buffer_11
  or or_4 (or_4_out, rst, or_6_out);
  register register_6 (
    .in_8(rst), .out_9(register_6_out_9), .in_1(data_in), .out_10(register_6_out_10),
    .out_11(register_6_out_11), .out_12(register_6_out_12), .out_13(register_6_out_13),
    .out_14(register_6_out_14), .out_15(data_addr), .out_16(register_6_out_16), .in_5(reg_1_t),
    .in_2(alu_1_out_15), .in_3(alu_1_out_16), .in_7(_4), .in_6(not_4_out), .in_4(alu_1_out_17));
  // Probe on register_6_out_16
  Counter counter_1 (
    .load(or_4_out), .D(controlled_buffer_9_out), .count(not_5_out), .Q(ip), .carry(out_3),
    .clk(buffer_7_out), .clr(1'b0));
  buf buffer_7 (buffer_7_out, or_5_out);
  or or_5 (or_5_out, rst, _1);
  xor xor_1 (xor_1_out, register_6_out_16[3], register_6_out_16[2]);
  nor nor_1 (nor_1_out, xor_1_out, register_6_out_16[1]);
  and and_6 (and_6_out, xor_1_out, jl);
  and and_7 (and_7_out, nor_1_out, jg);
  assign addr_t = ram1 ? multiplexer_1_out : 8'bz;  // Controlled_Buffer controlled_buffer_12
  Multiplexer #(.select(3), .width(8)) multiplexer_1 (
    .in1(register_6_out_9), .in2(register_6_out_10), .in3(register_6_out_11), .in4(register_6_out_12),
    .in5(register_6_out_13), .in6(register_6_out_14), .in7(data_addr), .out(multiplexer_1_out), .sel(reg_1),
    .en(not_6_out));  // open: in0
  not not_6 (not_6_out, all_1);
  Multiplexer #(.select(3), .width(8)) multiplexer_2 (
    .in1(register_6_out_9), .in2(register_6_out_10), .in3(register_6_out_11), .in4(register_6_out_12),
    .in5(register_6_out_13), .in6(register_6_out_14), .in7(data_addr), .out(multiplexer_2_out), .sel(reg_2),
    .en(all_0));  // open: in0
  assign addr_t = ram2 ? multiplexer_2_out : 8'bz;  // Controlled_Buffer controlled_buffer_13
  and and_8 (and_8_out, register_6_out_16[1], je);
  or or_6 (or_6_out, and_6_out, and_7_out, and_8_out, and_9_out, and_10_out, jmp_t);
  assign data_in = not_9_out ? controlled_buffer_19_out : 8'bz;  // Controlled_Buffer controlled_buffer_14
  assign controlled_buffer_15_out = not_7_out ? multiplexer_2_out : 8'bz;  // Controlled_Buffer controlled_buffer_15
  not not_7 (not_7_out, ram2);
  nor nor_2 (nor_2_out, register_6_out_16[1], register_6_out_16[0]);
  and and_9 (and_9_out, nor_2_out, ujg);
  and and_10 (and_10_out, register_6_out_16[0], ujl);
  assign controlled_buffer_8_out = not_8_out ? controlled_buffer_18_out : 8'bz;  // Controlled_Buffer controlled_buffer_16
  not not_8 (not_8_out, ram1);
  not not_9 (not_9_out, dire_t);
  assign controlled_buffer_8_out = not_10_out ? controlled_buffer_22_out : 8'bz;  // Controlled_Buffer controlled_buffer_17
  assign controlled_buffer_18_out = dire_t ? controlled_buffer_19_out : 8'bz;  // Controlled_Buffer controlled_buffer_18
  assign controlled_buffer_19_out = register_7_q ? multiplexer_1_out : 8'bz;  // Controlled_Buffer controlled_buffer_19
  assign controlled_buffer_8_out = register_7_q ? controlled_buffer_15_out : 8'bz;  // Controlled_Buffer controlled_buffer_20
  Register #(.width(1)) register_7 (.D(1'b1), .en(_2), .Q(register_7_q), .clk(_2), .clr(_3));
  not not_10 (not_10_out, dire_t);
  assign data_in = dire_t ? controlled_buffer_22_out : 8'bz;  // Controlled_Buffer controlled_buffer_21
  assign controlled_buffer_22_out = register_7_q ? controlled_buffer_23_out : 8'bz;  // Controlled_Buffer controlled_buffer_22
  assign controlled_buffer_23_out = or_8_out ? data_out : 8'bz;  // Controlled_Buffer controlled_buffer_23
  nor nor_3 (nor_3_out, all_1, set, all_0);
  or or_7 (or_7_out, ram1, ram2);
  and and_11 (and_11_out, or_8_out, dire_t);
  not not_11 (not_11_out, prt);
  Register register_8 (
    .D(register_6_out_14), .en(controlled_buffer_24_out), .Q(cs), .clk(controlled_buffer_24_out), .clr(rst));
  assign controlled_buffer_24_out = or_6_out ? _1 : 1'bz;  // Controlled_Buffer controlled_buffer_24
  or or_8 (or_8_out, nor_3_out, or_7_out);
  Pull_Resistor pull_resistor_5 (.node(str));
  assign str = not_11_out ? and_11_out : 1'bz;  // Controlled_Buffer controlled_buffer_25
  RAM_part #(.addrWidth(16), .bus("separate")) ram_2 (
    .addr({data_addr, addr_t}), .din(data_in), .data(data_out), .str(str), .sel(1'b1), .clk(_4), .ld(1'b1),
    .clr(rst));

  // Other names for the same wires on the sheet: clk = _4; data_addr[7:0] = addr_t; instruction[11] = dire

  // Notes on the sheet:
  //   blend
  //   immediately
  //   address
  //   reg addr
  //   reg addr
  //   opcode
  //   direction
  //   opcode
  //   opcode
  //   O S Z C
  //   IN
  //   OUT
  //   STR
  //   CLK
  //   RST
  //   ADDRESS
endmodule

module CPU (
  input  [7:0] in_1,
  input  [15:0] in_2,
  input  rst,
  input  clk,
  output [7:0] out_5,
  output [7:0] out_6,
  output STR,
  output CLK_2,
  output RST_2,
  output out_10,
  output [15:0] ADDRESS,
  output [15:0] out_12
);

  wire _1, _2, _3, add, add_t, all_0, all_1, alu_1_out_16, \and , and_1_out, and_2_out, and_3_out, and_6_out,
       and_7_out, and_8_out, and_9_out, and_10_out, and_11_out, and_t, buffer_6_out, buffer_7_out, cmp,
       cmp_t, controlled_buffer_24_out, dire_t, div, div_t, imme, imme_t, je, jg, jl, jmp, jmp_t, mov, mul,
       mul_t, nor_1_out, nor_2_out, nor_3_out, \not , not_2_out, not_3_out, not_4_out, not_5_out, not_6_out,
       not_7_out, not_8_out, not_9_out, not_10_out, not_11_out, not_t, \or , or_1_out, or_2_out, or_3_out,
       or_4_out, or_5_out, or_6_out, or_7_out, or_8_out, or_t, prt, ram1, ram2, register_4_q, register_7_q,
       rst_t, set, shf, shf_t, sub, sub_t, ujg, ujl, xnor_1_out, xnor_2_out, \xor , xor_1_out, xor_t;
  wire [2:0] opcode_2, opcode_2_t, reg_1, reg_1_t, reg_2;
  wire [3:0] alu_1_out_17, controlled_buffer_4_out, not_1_out, register_6_out_16;
  wire [7:0] addr, alu_1_out_14, alu_1_out_15, controlled_buffer_2_out, controlled_buffer_8_out,
       controlled_buffer_9_out, controlled_buffer_10_out, controlled_buffer_15_out, controlled_buffer_17_out,
       controlled_buffer_18_out, controlled_buffer_22_out, controlled_buffer_23_out, multiplexer_1_out,
       multiplexer_2_out, num, num_t, register_2_q, register_3_q, register_5_q, register_6_out_9,
       register_6_out_10, register_6_out_11, register_6_out_12, register_6_out_13, register_6_out_14;

  assign num = imme_t ? in_2[7:0] : 8'bz;  // Controlled_Buffer controlled_buffer_1
  xnor xnor_1 (xnor_1_out, imme_t, all_0);
  assign controlled_buffer_2_out = all_0 ? in_2[7:0] : 8'bz;  // Controlled_Buffer controlled_buffer_2
  assign opcode_2 = all_1 ? in_2[10:8] : 3'bz;  // Controlled_Buffer controlled_buffer_3
  assign controlled_buffer_4_out = xnor_2_out ? in_2[15:12] : 4'bz;  // Controlled_Buffer controlled_buffer_4
  assign not_1_out = ~in_2[15:12];  // NOT_Gate not_1, 4 bits wide
  Pull_Resistor pull_resistor_1 (.node(addr));
  assign addr = xnor_1_out ? in_2[7:0] : 8'bz;  // Controlled_Buffer controlled_buffer_5
  assign reg_2 = controlled_buffer_2_out[2:0];  // Buffer buffer_1, 3 bits wide
  assign controlled_buffer_4_out = controlled_buffer_2_out[7:4];  // Buffer buffer_2, 4 bits wide
  Pull_Resistor pull_resistor_2 (.node(reg_1));
  assign reg_1 = not_2_out ? in_2[10:8] : 3'bz;  // Controlled_Buffer controlled_buffer_6
  not not_2 (not_2_out, all_1);
  xnor xnor_2 (xnor_2_out, all_1, all_0);
  and and_1 (and_1_out, not_1_out[0], not_1_out[1], not_1_out[2], not_1_out[3]);
  buf buffer_3 (all_0, and_1_out);
  buf buffer_4 (all_1, and_2_out);
  and and_2 (and_2_out, in_2[12], in_2[13], in_2[14], in_2[15]);
  buf buffer_5 (imme, and_3_out);
  and and_3 (and_3_out, in_2[12], in_2[14], in_2[15]);
  Register register_1 (.D(out_6), .en(prt), .Q(out_5), .clk(CLK_2), .clr(rst_t));
  and and_4 (ram1, in_2[11], all_0);
  and and_5 (ram2, controlled_buffer_2_out[3], all_0);
  Decoder #(.select(4), .enable("false")) decoder_1 (
    .out1(add), .out2(sub), .out3(mul), .out4(div), .out5(\and ), .out6(\or ), .out7(\xor ), .out8(shf),
    .out9(cmp), .out10(mov), .out11(\not ), .out12(prt), .out13(set), .sel(controlled_buffer_4_out));  // open: out0, out14, out15
  Pull_Resistor pull_resistor_3 (.node(controlled_buffer_4_out));
  Register register_2 (.D(out_6), .en(_3), .Q(register_2_q), .clk(_3), .clr(rst_t));
  ALU alu_1 (
    .in_12(register_2_q), .ADD_2(register_3_q), .out_14(alu_1_out_14), .out_15(alu_1_out_15),
    .out_16(alu_1_out_16), .ADD(add_t), .SUB(sub_t), .MUL(mul_t), .DIV(div_t), .AND(and_t), .OR(or_t),
    .XOR(xor_t), .SHF(shf_t), .CMP(cmp_t), .NOT(not_t), .out_17(alu_1_out_17), .MOV(or_1_out));
  Register register_3 (.D(controlled_buffer_9_out), .en(_3), .Q(register_3_q), .clk(_3), .clr(rst_t));
  or or_1 (or_1_out, set, prt, mov);
  Pull_Resistor pull_resistor_4 (.node(opcode_2_t));
  Decoder #(.select(3), .enable("false")) decoder_2 (
    .out1(jmp), .out2(je), .out3(jg), .out4(jl), .out5(ujg), .out6(ujl), .sel(opcode_2_t));  // open: out0, out7
  Register #(.width(1)) register_4 (.D(1'b1), .en(_3), .Q(register_4_q), .clk(_3), .clr(CLK_2));
  clock clock_1 (.out_5(CLK_2), .out_4(_1), .out_3(_3), .out_6(_2), .in_2(rst_t), .in_1(clk));
  assign out_6 = buffer_6_out ? alu_1_out_14 : 8'bz;  // Controlled_Buffer controlled_buffer_7
  buf buffer_6 (buffer_6_out, register_4_q);
  assign controlled_buffer_8_out = or_4_out ? controlled_buffer_9_out : 8'bz;  // Controlled_Buffer controlled_buffer_8
  Register register_5 (.D(controlled_buffer_8_out), .en(CLK_2), .Q(register_5_q), .clk(CLK_2), .clr(rst_t));
  assign controlled_buffer_9_out = or_2_out ? num_t : 8'bz;  // Controlled_Buffer controlled_buffer_9
  or or_2 (or_2_out, set, all_1);
  or or_3 (or_3_out, prt, dire_t);
  not not_3 (not_3_out, or_3_out);
  assign controlled_buffer_10_out = not_4_out ? register_5_q : 8'bz;  // Controlled_Buffer controlled_buffer_10
  not not_4 (not_4_out, rst_t);
  assign controlled_buffer_10_out = rst_t ? {8{1'b1}} : 8'bz;  // Controlled_Buffer controlled_buffer_11
  or or_4 (or_4_out, rst_t, or_6_out);
  register register_6 (
    .in_8(rst), .out_9(register_6_out_9), .in_1(out_6), .out_10(register_6_out_10),
    .out_11(register_6_out_11), .out_12(register_6_out_12), .out_13(register_6_out_13),
    .out_14(register_6_out_14), .out_15(ADDRESS[15:8]), .out_16(register_6_out_16), .in_5(reg_1_t),
    .in_2(alu_1_out_15), .in_3(alu_1_out_16), .in_7(CLK_2), .in_6(not_3_out), .in_4(alu_1_out_17));
  // Probe on register_6_out_16
  Counter counter_1 (
    .load(or_4_out), .D(controlled_buffer_10_out), .count(not_5_out), .Q(out_12[7:0]), .carry(out_10),
    .clk(buffer_7_out), .clr(1'b0));
  not not_5 (not_5_out, or_4_out);
  buf buffer_7 (buffer_7_out, or_5_out);
  or or_5 (or_5_out, rst_t, _1);
  xor xor_1 (xor_1_out, register_6_out_16[3], register_6_out_16[2]);
  and and_6 (and_6_out, xor_1_out, jl);
  Multiplexer #(.select(3), .width(8)) multiplexer_1 (
    .in1(register_6_out_9), .in2(register_6_out_10), .in3(register_6_out_11), .in4(register_6_out_12),
    .in5(register_6_out_13), .in6(register_6_out_14), .in7(ADDRESS[15:8]), .out(multiplexer_1_out),
    .sel(reg_1), .en(not_6_out));  // open: in0
  not not_6 (not_6_out, all_1);
  Multiplexer #(.select(3), .width(8)) multiplexer_2 (
    .in1(register_6_out_9), .in2(register_6_out_10), .in3(register_6_out_11), .in4(register_6_out_12),
    .in5(register_6_out_13), .in6(register_6_out_14), .in7(ADDRESS[15:8]), .out(multiplexer_2_out),
    .sel(reg_2), .en(all_0));  // open: in0
  assign ADDRESS[7:0] = ram2 ? multiplexer_2_out : 8'bz;  // Controlled_Buffer controlled_buffer_12
  nor nor_1 (nor_1_out, xor_1_out, register_6_out_16[1]);
  and and_7 (and_7_out, nor_1_out, jg);
  and and_8 (and_8_out, register_6_out_16[1], je);
  or or_6 (or_6_out, and_6_out, and_7_out, and_8_out, and_9_out, and_10_out, jmp_t);
  assign ADDRESS[7:0] = ram1 ? multiplexer_1_out : 8'bz;  // Controlled_Buffer controlled_buffer_13
  assign out_6 = not_9_out ? controlled_buffer_18_out : 8'bz;  // Controlled_Buffer controlled_buffer_14
  assign controlled_buffer_15_out = not_7_out ? multiplexer_2_out : 8'bz;  // Controlled_Buffer controlled_buffer_15
  not not_7 (not_7_out, ram2);
  nor nor_2 (nor_2_out, register_6_out_16[1], register_6_out_16[0]);
  and and_9 (and_9_out, nor_2_out, ujg);
  assign controlled_buffer_9_out = not_8_out ? controlled_buffer_17_out : 8'bz;  // Controlled_Buffer controlled_buffer_16
  not not_8 (not_8_out, ram1);
  not not_9 (not_9_out, dire_t);
  assign controlled_buffer_17_out = dire_t ? controlled_buffer_18_out : 8'bz;  // Controlled_Buffer controlled_buffer_17
  assign controlled_buffer_18_out = register_7_q ? multiplexer_1_out : 8'bz;  // Controlled_Buffer controlled_buffer_18
  assign controlled_buffer_9_out = register_7_q ? controlled_buffer_15_out : 8'bz;  // Controlled_Buffer controlled_buffer_19
  Register #(.width(1)) register_7 (.D(1'b1), .en(_2), .Q(register_7_q), .clk(_2), .clr(_3));
  and and_10 (and_10_out, register_6_out_16[0], ujl);
  not not_10 (not_10_out, dire_t);
  assign controlled_buffer_9_out = not_10_out ? controlled_buffer_22_out : 8'bz;  // Controlled_Buffer controlled_buffer_20
  assign out_6 = dire_t ? controlled_buffer_22_out : 8'bz;  // Controlled_Buffer controlled_buffer_21
  assign controlled_buffer_22_out = register_7_q ? controlled_buffer_23_out : 8'bz;  // Controlled_Buffer controlled_buffer_22
  assign controlled_buffer_23_out = or_8_out ? in_1 : 8'bz;  // Controlled_Buffer controlled_buffer_23
  nor nor_3 (nor_3_out, all_1, set, all_0);
  or or_7 (or_7_out, ram1, ram2);
  and and_11 (and_11_out, or_8_out, dire_t);
  Register register_8 (
    .D(register_6_out_14), .en(controlled_buffer_24_out), .Q(out_12[15:8]), .clk(controlled_buffer_24_out),
    .clr(rst_t));
  assign controlled_buffer_24_out = or_6_out ? _1 : 1'bz;  // Controlled_Buffer controlled_buffer_24
  or or_8 (or_8_out, nor_3_out, or_7_out);
  not not_11 (not_11_out, prt);
  assign STR = not_11_out ? and_11_out : 1'bz;  // Controlled_Buffer controlled_buffer_25
  Pull_Resistor pull_resistor_5 (.node(STR));

  assign RST_2 = rst;

  // Other names for the same wires on the sheet: _4 = CLK_2; addr_t[7:0] = ADDRESS[7:0]; dire = in_2[11]

  // Notes on the sheet:
  //   instruction
  //   address
  //   blend
  //   address
  //   immediately
  //   reg addr
  //   reg addr
  //   opcode
  //   direction
  //   opcode
  //   opcode
  //   O S Z C
  //   IN
  //   OUT
endmodule
